# Fritzing sketch uno_timer (saved by Fritzing 0.9.4)
breadboards: 1

parts:
  Part1 = Arduino Uno (Rev3)
  J1 = Piezo Speaker
  S1 = Pushbutton [package="[THT]"]
  7_Segment_4_Digit_Display1 = 7-SEGMENT-4DIGIT common anode [part_number="5461BS - 5462BS" package=7-segment-4digit-anode]

nets:
  N1: Part1.A0, 7_Segment_4_Digit_Display1.pin_1
  N2: Part1.A1, 7_Segment_4_Digit_Display1.pin_2
  N3: Part1.A2, 7_Segment_4_Digit_Display1.pin_3
  N4: Part1.A3, 7_Segment_4_Digit_Display1.pin_4
  N5: Part1.A4/SDA, 7_Segment_4_Digit_Display1.pin_5
  N6: Part1.A5/SCL, 7_Segment_4_Digit_Display1.pin_6
  N7: Part1.D8, J1.pin2
  N8: Part1.D1/TX, 7_Segment_4_Digit_Display1.pin_7
  N9: Part1.D2, 7_Segment_4_Digit_Display1.pin_8
  N10: Part1.D3_PWM, 7_Segment_4_Digit_Display1.pin_9
  N11: Part1.D4, 7_Segment_4_Digit_Display1.pin_10
  N12: Part1.D5_PWM, 7_Segment_4_Digit_Display1.pin_11
  N13: Part1.D6_PWM, 7_Segment_4_Digit_Display1.pin_12
  N14: Part1.D7, S1.Pin_1, S1.Pin_2
  GND: Part1.GND, J1.pin1, S1.Pin_3, S1.Pin_4

custom parts:
  7-SEGMENT-4DIGIT common anode: A 7 Segment 4 Digit common anode display, with decimal points
